// Logisim project y86.circ as structural Verilog
module main (
  input  Reset
);

  wire and_1_out, Clock_out, nor_1_out, not_1_out;
  wire [1:0] imem_1_p12, Stat_q;
  wire [3:0] icode, ifun, rA, rB;
  wire [7:0] imem_1_p3, imem_1_p4, imem_1_p5, imem_1_p6, imem_1_p7, imem_1_p8, imem_1_p9, imem_1_p10,
       imem_1_p11;
  wire [31:0] PC_q, PChold_q, valc_0, valc_1;

  and and_1 (and_1_out, Clock_out, nor_1_out);
  Clock Clock (.out(Clock_out));
  Register #(.width(32)) PC (.D(PChold_q), .Q(PC_q), .clk(and_1_out), .clr(Reset));  // open: en
  nor nor_1 (nor_1_out, Stat_q[1], Stat_q[0]);
  not not_1 (not_1_out, and_1_out);
  Register #(.width(2)) Stat (.D(imem_1_p12), .Q(Stat_q), .clk(not_1_out));  // open: en, clr
  // imem imem_1: pin names not known; wires that end beside it: PC_q, {ifun, icode}, imem_1_p3, imem_1_p4, imem_1_p5, imem_1_p6, imem_1_p7, imem_1_p8, imem_1_p9, imem_1_p10, imem_1_p11, imem_1_p12
  Align align_1 (
    .B1(imem_1_p3), .B2(imem_1_p4), .B3(imem_1_p5), .B4(imem_1_p6), .B5(imem_1_p7), .B6(imem_1_p8),
    .B7(imem_1_p9), .B8(imem_1_p10), .B9(imem_1_p11), .rA(rA), .rB(rB), .valC_1(valc_1), .valC_0(valc_0));  // open: NeedRegs
  // regfile regfile_1: pin names not known; wires that end beside it: 4'b1111, rB, rB, valc_1, valc_0, 4'b1111, {32{1'b1}}, {32{1'b1}}
  Register #(.width(32)) PChold (.Q(PChold_q), .clk(not_1_out), .clr(Reset));  // open: D, en

  // Notes on the sheet:
  //   reg inputs temporary
endmodule

module Align (
  input  [7:0] B1,
  input  [7:0] B2,
  input  [7:0] B3,
  input  [7:0] B4,
  input  [7:0] B5,
  input  [7:0] B6,
  input  [7:0] B7,
  input  [7:0] B8,
  input  [7:0] B9,
  input  NeedRegs,
  output [3:0] rA,
  output [3:0] rB,
  output [31:0] valC_1,
  output [31:0] valC_0
);

  wire [3:0] icode;

  Multiplexer #(.select(4)) multiplexer_1 (
    .in0(1'b0), .in1(1'b0), .in2(1'b1), .in3(1'b1), .in4(1'b1), .in5(1'b1), .in6(1'b1), .in7(1'b0),
    .in8(1'b0), .in9(1'b0), .in10(1'b1), .in11(1'b1), .in12(1'b1), .in13(1'b1), .in14(1'b1), .in15(1'b1),
    .out(NeedRegs), .sel(icode));  // open: en

  assign rA = B1[3:0];
  assign rB = B1[7:4];
  assign valC_0 = {B5, B4, B3, B2};
  assign valC_1 = {B6, B7, B8, B9};
endmodule
